// Logisim project CLOCKA.circ as structural Verilog: 1 circuit, main circuit main
module main (
  output sec_clk
);

  wire clock_1_out, d_ff_1_q, d_ff_1_qn, d_ff_2_q, d_ff_2_qn, d_ff_3_q, d_ff_3_qn, d_ff_4_q, d_ff_4_qn,
       d_ff_5_q, d_ff_5_qn, d_ff_6_q, d_ff_6_qn, d_ff_7_q, d_ff_7_qn, d_ff_8_q, d_ff_8_qn, d_ff_9_q,
       d_ff_9_qn, d_ff_10_q, d_ff_10_qn, d_ff_11_q, d_ff_11_qn, d_ff_12_q, d_ff_12_qn, d_ff_13_q, d_ff_13_qn,
       d_ff_14_qn;

  Clock clock_1 (.out(clock_1_out));
  D_Flip_Flop d_ff_1 (.D(d_ff_1_qn), .clk(clock_1_out), .Q(d_ff_1_q), .Qn(d_ff_1_qn));  // open: preset, reset
  D_Flip_Flop d_ff_2 (.D(d_ff_2_qn), .clk(d_ff_1_q), .Q(d_ff_2_q), .Qn(d_ff_2_qn));  // open: preset, reset
  D_Flip_Flop d_ff_3 (.D(d_ff_3_qn), .clk(d_ff_2_q), .Q(d_ff_3_q), .Qn(d_ff_3_qn));  // open: preset, reset
  D_Flip_Flop d_ff_4 (.D(d_ff_4_qn), .clk(d_ff_3_q), .Q(d_ff_4_q), .Qn(d_ff_4_qn));  // open: preset, reset
  D_Flip_Flop d_ff_5 (.D(d_ff_5_qn), .clk(d_ff_4_q), .Q(d_ff_5_q), .Qn(d_ff_5_qn));  // open: preset, reset
  D_Flip_Flop d_ff_6 (.D(d_ff_6_qn), .clk(d_ff_5_q), .Q(d_ff_6_q), .Qn(d_ff_6_qn));  // open: preset, reset
  D_Flip_Flop d_ff_7 (.D(d_ff_7_qn), .clk(d_ff_6_q), .Q(d_ff_7_q), .Qn(d_ff_7_qn));  // open: preset, reset
  D_Flip_Flop d_ff_8 (.D(d_ff_8_qn), .clk(d_ff_7_q), .Q(d_ff_8_q), .Qn(d_ff_8_qn));  // open: preset, reset
  D_Flip_Flop d_ff_9 (.D(d_ff_9_qn), .clk(d_ff_8_q), .Q(d_ff_9_q), .Qn(d_ff_9_qn));  // open: preset, reset
  D_Flip_Flop d_ff_10 (.D(d_ff_10_qn), .clk(d_ff_9_q), .Q(d_ff_10_q), .Qn(d_ff_10_qn));  // open: preset, reset
  D_Flip_Flop d_ff_11 (.D(d_ff_11_qn), .clk(d_ff_10_q), .Q(d_ff_11_q), .Qn(d_ff_11_qn));  // open: preset, reset
  D_Flip_Flop d_ff_12 (.D(d_ff_12_qn), .clk(d_ff_11_q), .Q(d_ff_12_q), .Qn(d_ff_12_qn));  // open: preset, reset
  D_Flip_Flop d_ff_13 (.D(d_ff_13_qn), .clk(d_ff_12_q), .Q(d_ff_13_q), .Qn(d_ff_13_qn));  // open: preset, reset
  D_Flip_Flop d_ff_14 (.D(d_ff_14_qn), .clk(d_ff_13_q), .Q(sec_clk), .Qn(d_ff_14_qn));  // open: preset, reset
endmodule
