// Logisim project guia02.circ as structural Verilog: 25 circuits, main circuit E06
module E06 (
  input  A,
  input  B,
  input  C,
  output s
);

  wire and_1_out, and_2_out, not_1_out;

  not not_1 (not_1_out, B);
  and and_1 (and_1_out, not_1_out, A);
  and and_2 (and_2_out, C, B);
  or or_1 (s, and_1_out, and_2_out);
endmodule

module dmux_1_4_E07 (
  input  c0,
  input  c1,
  input  e,
  output s0,
  output s1,
  output s2,
  output s3
);

  wire and_2_out, and_4_out, and_6_out, and_8_out, not_1_out, not_2_out, not_3_out, not_4_out;

  not not_1 (not_1_out, c0);
  not not_2 (not_2_out, c1);
  not not_3 (not_3_out, c1);
  not not_4 (not_4_out, c0);
  and and_1 (s0, e, and_2_out);
  and and_2 (and_2_out, not_1_out, not_2_out);
  and and_3 (s1, e, and_4_out);
  and and_4 (and_4_out, c0, not_3_out);
  and and_5 (s2, e, and_6_out);
  and and_6 (and_6_out, not_4_out, c1);
  and and_7 (s3, e, and_8_out);
  and and_8 (and_8_out, c0, c1);
endmodule

module encoder_4_2_E08 (
  input  e0,
  input  e1,
  input  e2,
  input  e3,
  output s0,
  output s1,
  output I
);

  wire and_1_out, and_2_out, and_3_out, and_4_out, and_5_out, and_6_out, and_7_out, and_8_out, and_9_out,
       not_1_out, not_2_out, not_3_out, not_4_out, not_5_out, not_6_out, not_7_out, not_8_out, not_9_out,
       or_3_out, or_4_out, or_5_out;

  or or_1 (s0, e1, e3);
  or or_2 (s1, e3, e2);
  not not_1 (not_1_out, e1);
  not not_2 (not_2_out, e0);
  not not_3 (not_3_out, e2);
  not not_4 (not_4_out, e1);
  not not_5 (not_5_out, e3);
  not not_6 (not_6_out, e2);
  and and_1 (and_1_out, e0, not_1_out);
  and and_2 (and_2_out, and_1_out, not_7_out);
  not not_7 (not_7_out, e2);
  not not_8 (not_8_out, e3);
  and and_3 (and_3_out, e1, not_3_out);
  and and_4 (and_4_out, and_3_out, not_9_out);
  not not_9 (not_9_out, e3);
  and and_5 (and_5_out, e2, not_5_out);
  and and_6 (and_6_out, not_6_out, e3);
  and and_7 (and_7_out, and_2_out, not_8_out);
  and and_8 (and_8_out, not_4_out, or_3_out);
  or or_3 (or_3_out, and_5_out, and_6_out);
  or or_4 (or_4_out, and_4_out, and_8_out);
  and and_9 (and_9_out, not_2_out, or_4_out);
  or or_5 (or_5_out, and_7_out, and_9_out);
  not not_10 (I, or_5_out);
endmodule

module decoder_2_4_E09A (
  input  e0,
  input  e1,
  output s0,
  output s1,
  output s2,
  output s3
);

  wire not_1_out, not_2_out, not_3_out, not_4_out;

  not not_1 (not_1_out, e0);
  not not_2 (not_2_out, e1);
  not not_3 (not_3_out, e1);
  not not_4 (not_4_out, e0);
  and and_1 (s0, not_1_out, not_2_out);
  and and_2 (s1, e0, not_3_out);
  and and_3 (s2, not_4_out, e1);
  and and_4 (s3, e0, e1);
endmodule

module dmux_1_4_E09B (
  input  c0,
  input  c1,
  input  e,
  output s0,
  output s1,
  output s2,
  output s3
);

  wire decoder_2_4_e09a_1_s0, decoder_2_4_e09a_1_s1, decoder_2_4_e09a_1_s2, decoder_2_4_e09a_1_s3;

  decoder_2_4_E09A decoder_2_4_e09a_1 (
    .e0(c0), .e1(c1), .s0(decoder_2_4_e09a_1_s0), .s1(decoder_2_4_e09a_1_s1), .s2(decoder_2_4_e09a_1_s2),
    .s3(decoder_2_4_e09a_1_s3));
  and and_1 (s0, decoder_2_4_e09a_1_s0, e);
  and and_2 (s1, decoder_2_4_e09a_1_s1, e);
  and and_3 (s2, decoder_2_4_e09a_1_s2, e);
  and and_4 (s3, decoder_2_4_e09a_1_s3, e);
endmodule

module left_shifter_3_4_E10 (
  input  e0,
  input  e1,
  input  e2,
  input  c,
  output s0,
  output s1,
  output s2,
  output s3
);

  wire and_2_out, and_3_out, and_4_out, and_5_out, not_1_out, not_2_out, not_3_out;

  not not_1 (not_1_out, c);
  not not_2 (not_2_out, c);
  not not_3 (not_3_out, c);
  and and_1 (s0, not_1_out, e0);
  and and_2 (and_2_out, not_2_out, e1);
  and and_3 (and_3_out, c, e0);
  and and_4 (and_4_out, not_3_out, e2);
  and and_5 (and_5_out, c, e1);
  and and_6 (s3, c, e2);
  or or_1 (s1, and_2_out, and_3_out);
  or or_2 (s2, and_4_out, and_5_out);
endmodule

module reg_4_E16 (
  input  i0,
  input  i1,
  input  i2,
  input  i3,
  input  load,
  output o0,
  output o1,
  output o2,
  output o3
);

  wire clock_1_out, multiplexer_1_out, multiplexer_2_out, multiplexer_3_out, multiplexer_4_out;

  D_Flip_Flop d_ff_1 (.D(multiplexer_1_out), .clk(clock_1_out), .Q(o0));  // open: Qn, preset, reset
  Multiplexer multiplexer_1 (.in0(o0), .in1(i0), .out(multiplexer_1_out), .sel(load));
  D_Flip_Flop d_ff_2 (.D(multiplexer_2_out), .clk(clock_1_out), .Q(o1));  // open: Qn, preset, reset
  Multiplexer multiplexer_2 (.in0(o1), .in1(i1), .out(multiplexer_2_out), .sel(load));
  D_Flip_Flop d_ff_3 (.D(multiplexer_3_out), .clk(clock_1_out), .Q(o2));  // open: Qn, preset, reset
  Multiplexer multiplexer_3 (.in0(o2), .in1(i2), .out(multiplexer_3_out), .sel(load));
  D_Flip_Flop d_ff_4 (.D(multiplexer_4_out), .clk(clock_1_out), .Q(o3));  // open: Qn, preset, reset
  Multiplexer multiplexer_4 (.in0(o3), .in1(i3), .out(multiplexer_4_out), .sel(load));
  Clock clock_1 (.out(clock_1_out));
endmodule

module reg_extensor_de_signo_4_E17 (
  input  i0,
  input  i1,
  input  i2,
  input  i3,
  input  load,
  input  ext,
  output o0,
  output o1,
  output o2,
  output o3
);

  wire [3:0] reg_4_e16_1_o2;

  reg_4_E16 reg_4_e16_1 (
    .i0(i0), .i1(i1), .i2(i2), .i3(i3), .load(load), .o0(reg_4_e16_1_o2[0]), .o1(reg_4_e16_1_o2[1]),
    .o2(reg_4_e16_1_o2[2]), .o3(reg_4_e16_1_o2[3]));
  Multiplexer #(.width(4)) multiplexer_1 (
    .in0(reg_4_e16_1_o2), .in1({{3{reg_4_e16_1_o2[1]}}, reg_4_e16_1_o2[0]}), .out({o3, o2, o1, o0}), .sel(ext));
endmodule

module reg_salida_restringida_4_E18 (
  input  i0,
  input  i1,
  input  i2,
  input  i3,
  input  load,
  input  read,
  output o0,
  output o1,
  output o2,
  output o3
);

  wire clock_1_out, d_ff_1_q;
  wire [3:0] reg_4_e16_1_o0;

  D_Flip_Flop d_ff_1 (.D(read), .clk(clock_1_out), .Q(d_ff_1_q));  // open: Qn, preset, reset
  Clock clock_1 (.out(clock_1_out));
  reg_4_E16 reg_4_e16_1 (
    .i0(i0), .i1(i1), .i2(i2), .i3(i3), .load(load), .o0(reg_4_e16_1_o0[0]), .o1(reg_4_e16_1_o0[1]),
    .o2(reg_4_e16_1_o0[2]), .o3(reg_4_e16_1_o0[3]));
  assign {o3, o2, o1, o0} = d_ff_1_q ? reg_4_e16_1_o0 : 4'bz;  // Controlled_Buffer controlled_buffer_1
endmodule

module reg_bidireccional_4_E19 (
  input  [3:0] in_4,
  input  load,
  input  read,
  output [3:0] out_4
);

  wire [3:0] controlled_buffer_1_out, reg_4_e16_1_o0;

  assign controlled_buffer_1_out = load ? in_4 : 4'bz;  // Controlled_Buffer controlled_buffer_1
  assign out_4 = read ? reg_4_e16_1_o0 : 4'bz;  // Controlled_Buffer controlled_buffer_2
  reg_4_E16 reg_4_e16_1 (
    .i0(controlled_buffer_1_out[0]), .i1(controlled_buffer_1_out[1]), .i2(controlled_buffer_1_out[2]),
    .i3(controlled_buffer_1_out[3]), .load(load), .o0(reg_4_e16_1_o0[0]), .o1(reg_4_e16_1_o0[1]),
    .o2(reg_4_e16_1_o0[2]), .o3(reg_4_e16_1_o0[3]));
endmodule

module ALU_reg_4_E20 (
  input  B3,
  input  B2,
  input  B1,
  input  B0,
  input  A3,
  input  A2,
  input  A1,
  input  A0,
  input  load_B,
  input  load_A,
  input  add,
  input  sub,
  input  and_log,
  input  or_log,
  input  read_out,
  output V,
  output C,
  output N,
  output Z,
  output o0,
  output o1,
  output o2,
  output o3
);

  wire [1:0] encoder_4_2_e08_1_s0;
  wire [3:0] alu_4_1_s, reg_4_e16_1_o0, reg_4_e16_2_o0;

  reg_4_E16 reg_4_e16_1 (
    .i0(B0), .i1(B1), .i2(B2), .i3(B3), .load(load_B), .o0(reg_4_e16_1_o0[0]), .o1(reg_4_e16_1_o0[1]),
    .o2(reg_4_e16_1_o0[2]), .o3(reg_4_e16_1_o0[3]));
  reg_4_E16 reg_4_e16_2 (
    .i0(A0), .i1(A1), .i2(A2), .i3(A3), .load(load_A), .o0(reg_4_e16_2_o0[0]), .o1(reg_4_e16_2_o0[1]),
    .o2(reg_4_e16_2_o0[2]), .o3(reg_4_e16_2_o0[3]));
  encoder_4_2_E08 encoder_4_2_e08_1 (
    .e0(add), .e1(sub), .e2(and_log), .e3(or_log), .s0(encoder_4_2_e08_1_s0[0]), .s1(encoder_4_2_e08_1_s0[1]));  // open: I
  ALU_4 alu_4_1 (
    .A(reg_4_e16_2_o0), .B(reg_4_e16_1_o0), .OP(encoder_4_2_e08_1_s0), .V(V), .C(C), .S(alu_4_1_s), .N(N),
    .Z(Z));
  reg_salida_restringida_4_E18 reg_salida_restringida_4_e18_1 (
    .i0(alu_4_1_s[0]), .i1(alu_4_1_s[1]), .i2(alu_4_1_s[2]), .i3(alu_4_1_s[3]), .load(1'b1), .read(read_out),
    .o0(o0), .o1(o1), .o2(o2), .o3(o3));
endmodule

module sumador_6_E23 (
  input  [5:0] A,
  input  [5:0] B,
  input  Cin,
  output [5:0] S,
  output Cout
);

  wire sumador_completo_1_1_cout, sumador_completo_1_2_cout, sumador_completo_1_3_cout,
       sumador_completo_1_4_cout, sumador_completo_1_5_cout;

  sumador_completo_1 sumador_completo_1_1 (.Cin(Cin), .A(A[0]), .B(B[0]), .S(S[0]), .Cout(sumador_completo_1_1_cout));
  sumador_completo_1 sumador_completo_1_2 (
    .Cin(sumador_completo_1_1_cout), .A(A[1]), .B(B[1]), .S(S[1]), .Cout(sumador_completo_1_2_cout));
  sumador_completo_1 sumador_completo_1_3 (
    .Cin(sumador_completo_1_2_cout), .A(A[2]), .B(B[2]), .S(S[2]), .Cout(sumador_completo_1_3_cout));
  sumador_completo_1 sumador_completo_1_4 (
    .Cin(sumador_completo_1_3_cout), .A(A[3]), .B(B[3]), .S(S[3]), .Cout(sumador_completo_1_4_cout));
  sumador_completo_1 sumador_completo_1_5 (
    .Cin(sumador_completo_1_4_cout), .A(A[4]), .B(B[4]), .S(S[4]), .Cout(sumador_completo_1_5_cout));
  sumador_completo_1 sumador_completo_1_6 (.Cin(sumador_completo_1_5_cout), .A(A[5]), .B(B[5]), .S(S[5]), .Cout(Cout));
endmodule

module decrementador_6_E23 (
  input  [5:0] A,
  output [5:0] S
);

  sumador_6_E23 sumador_6_e23_1 (.A(A), .B({6{1'b1}}), .Cin(1'b0), .S(S));  // open: Cout
endmodule

module reg_restador_6_E23A (
  input  enable,
  input  RESET,
  output [5:0] S
);

  wire clock_1_out, multiplexer_1_out, multiplexer_2_out, multiplexer_3_out, multiplexer_4_out,
       multiplexer_5_out, multiplexer_6_out;
  wire [5:0] decrementador_6_e23_1_s;

  D_Flip_Flop d_ff_1 (.D(multiplexer_1_out), .clk(clock_1_out), .Q(S[0]), .reset(RESET));  // open: Qn, preset
  Multiplexer multiplexer_1 (.in0(S[0]), .in1(decrementador_6_e23_1_s[0]), .out(multiplexer_1_out), .sel(enable));
  D_Flip_Flop d_ff_2 (.D(multiplexer_2_out), .clk(clock_1_out), .Q(S[1]), .preset(RESET));  // open: Qn, reset
  Multiplexer multiplexer_2 (.in0(S[1]), .in1(decrementador_6_e23_1_s[1]), .out(multiplexer_2_out), .sel(enable));
  D_Flip_Flop d_ff_3 (.D(multiplexer_3_out), .clk(clock_1_out), .Q(S[2]), .preset(RESET));  // open: Qn, reset
  Multiplexer multiplexer_3 (.in0(S[2]), .in1(decrementador_6_e23_1_s[2]), .out(multiplexer_3_out), .sel(enable));
  D_Flip_Flop d_ff_4 (.D(multiplexer_4_out), .clk(clock_1_out), .Q(S[3]), .preset(RESET));  // open: Qn, reset
  Multiplexer multiplexer_4 (.in0(S[3]), .in1(decrementador_6_e23_1_s[3]), .out(multiplexer_4_out), .sel(enable));
  D_Flip_Flop d_ff_5 (.D(multiplexer_5_out), .clk(clock_1_out), .Q(S[4]), .preset(RESET));  // open: Qn, reset
  Multiplexer multiplexer_5 (.in0(S[4]), .in1(decrementador_6_e23_1_s[4]), .out(multiplexer_5_out), .sel(enable));
  D_Flip_Flop d_ff_6 (.D(multiplexer_6_out), .clk(clock_1_out), .Q(S[5]), .reset(RESET));  // open: Qn, preset
  Multiplexer multiplexer_6 (.in0(S[5]), .in1(decrementador_6_e23_1_s[5]), .out(multiplexer_6_out), .sel(enable));
  Clock clock_1 (.out(clock_1_out));
  decrementador_6_E23 decrementador_6_e23_1 (.A(S), .S(decrementador_6_e23_1_s));
endmodule

module a_mayor_b_16_E23 (
  input  [15:0] B,
  input  [15:0] A,
  output GE
);

  wire a_mayor_b_sin_signo_4_1_p3, a_mayor_b_sin_signo_4_2_p3, a_mayor_b_sin_signo_4_3_p3,
       a_mayor_b_sin_signo_4_4_p3, and_1_out, and_2_out, and_3_out, and_4_out, and_5_out, igualdad_4_1_i,
       igualdad_4_2_i, igualdad_4_3_i, or_1_out, or_2_out;

  igualdad_4 igualdad_4_1 (.A(A[15:12]), .B(B[15:12]), .I(igualdad_4_1_i));
  // a_mayor_b_sin_signo_4 a_mayor_b_sin_signo_4_1: pin names not known; wires that end beside it: A[15:12], B[15:12], a_mayor_b_sin_signo_4_1_p3
  igualdad_4 igualdad_4_2 (.A(A[11:8]), .B(B[11:8]), .I(igualdad_4_2_i));
  // a_mayor_b_sin_signo_4 a_mayor_b_sin_signo_4_2: pin names not known; wires that end beside it: A[11:8], B[11:8], a_mayor_b_sin_signo_4_2_p3
  igualdad_4 igualdad_4_3 (.A(A[7:4]), .B(B[7:4]), .I(igualdad_4_3_i));
  // a_mayor_b_sin_signo_4 a_mayor_b_sin_signo_4_3: pin names not known; wires that end beside it: A[7:4], B[7:4], a_mayor_b_sin_signo_4_3_p3
  // a_mayor_b_sin_signo_4 a_mayor_b_sin_signo_4_4: pin names not known; wires that end beside it: A[3:0], B[3:0], a_mayor_b_sin_signo_4_4_p3
  and and_1 (and_1_out, igualdad_4_1_i, a_mayor_b_sin_signo_4_2_p3);
  and and_2 (and_2_out, igualdad_4_1_i, igualdad_4_2_i);
  and and_3 (and_3_out, and_2_out, a_mayor_b_sin_signo_4_3_p3);
  and and_4 (and_4_out, and_2_out, igualdad_4_3_i);
  or or_1 (or_1_out, a_mayor_b_sin_signo_4_1_p3, and_1_out);
  and and_5 (and_5_out, and_4_out, a_mayor_b_sin_signo_4_4_p3);
  or or_2 (or_2_out, or_1_out, and_3_out);
  or or_3 (GE, or_2_out, and_5_out);
endmodule

module a_mayorigual_6000_16_E23B (
  input  [15:0] A,
  output GE
);

  a_mayor_b_16_E23 a_mayor_b_16_e23_1 (.B(16'h176f), .A(A), .GE(GE));
endmodule

module lavarropas_E23C (
  input  [15:0] carga,
  input  START_PAUSE,
  output [5:0] timer
);

  wire a_mayorigual_6000_16_e23b_1_ge, and_1_out, and_2_out, and_3_out, comparador_cero_4_1_z,
       comparador_cero_4_2_z, not_1_out, not_2_out, RESET_out;

  Button RESET (.out(RESET_out));
  not not_1 (not_1_out, a_mayorigual_6000_16_e23b_1_ge);
  a_mayorigual_6000_16_E23B a_mayorigual_6000_16_e23b_1 (.A(carga), .GE(a_mayorigual_6000_16_e23b_1_ge));
  and and_1 (and_1_out, not_1_out, START_PAUSE);
  and and_2 (and_2_out, and_1_out, not_2_out);
  not not_2 (not_2_out, and_3_out);
  reg_restador_6_E23A reg_restador_6_e23a_1 (.enable(and_2_out), .RESET(RESET_out), .S(timer));
  comparador_cero_4 comparador_cero_4_1 (.A(timer[3:0]), .Z(comparador_cero_4_1_z));
  comparador_cero_4 comparador_cero_4_2 (.A({2'b00, timer[5:4]}), .Z(comparador_cero_4_2_z));
  and and_3 (and_3_out, comparador_cero_4_1_z, comparador_cero_4_2_z);
endmodule

module par_5_E24 (
  input  [4:0] A,
  output P
);

  not not_1 (P, A[0]);
endmodule

module sumador_5_E24 (
  input  [4:0] A,
  input  [4:0] B,
  input  Cin,
  output [4:0] S,
  output Cout
);

  wire sumador_completo_1_1_cout, sumador_completo_1_2_cout, sumador_completo_1_3_cout,
       sumador_completo_1_4_cout;

  sumador_completo_1 sumador_completo_1_1 (.Cin(Cin), .A(A[0]), .B(B[0]), .S(S[0]), .Cout(sumador_completo_1_1_cout));
  sumador_completo_1 sumador_completo_1_2 (
    .Cin(sumador_completo_1_1_cout), .A(A[1]), .B(B[1]), .S(S[1]), .Cout(sumador_completo_1_2_cout));
  sumador_completo_1 sumador_completo_1_3 (
    .Cin(sumador_completo_1_2_cout), .A(A[2]), .B(B[2]), .S(S[2]), .Cout(sumador_completo_1_3_cout));
  sumador_completo_1 sumador_completo_1_4 (
    .Cin(sumador_completo_1_3_cout), .A(A[3]), .B(B[3]), .S(S[3]), .Cout(sumador_completo_1_4_cout));
  sumador_completo_1 sumador_completo_1_5 (.Cin(sumador_completo_1_4_cout), .A(A[4]), .B(B[4]), .S(S[4]), .Cout(Cout));
endmodule

module triplicador_incrementador_5_E24 (
  input  [4:0] A,
  output [4:0] S
);

  wire sumador_5_e24_1_cout;
  wire [4:0] sumador_5_e24_1_s;

  sumador_5_E24 sumador_5_e24_1 (.A(A), .B(A), .Cin(1'b1), .S(sumador_5_e24_1_s), .Cout(sumador_5_e24_1_cout));
  sumador_5_E24 sumador_5_e24_2 (.A(sumador_5_e24_1_s), .B(A), .Cin(sumador_5_e24_1_cout), .S(S));  // open: Cout
endmodule

module right_shifter_4_5_E24 (
  input  e0,
  input  e1,
  input  e2,
  input  e3,
  input  c,
  output s0,
  output s1,
  output s2,
  output s3,
  output s4
);

  wire and_2_out, and_3_out, and_4_out, and_5_out, and_6_out, and_7_out, not_1_out, not_2_out, not_3_out,
       not_4_out;

  not not_1 (not_1_out, c);
  not not_2 (not_2_out, c);
  not not_3 (not_3_out, c);
  not not_4 (not_4_out, c);
  and and_1 (s0, c, e0);
  and and_2 (and_2_out, not_1_out, e0);
  and and_3 (and_3_out, c, e1);
  and and_4 (and_4_out, not_2_out, e1);
  and and_5 (and_5_out, c, e2);
  and and_6 (and_6_out, not_3_out, e2);
  and and_7 (and_7_out, c, e3);
  and and_8 (s4, not_4_out, e3);
  or or_1 (s1, and_2_out, and_3_out);
  or or_2 (s2, and_4_out, and_5_out);
  or or_3 (s3, and_6_out, and_7_out);
endmodule

module comparador_cero_5_E24 (
  input  [4:0] A,
  output Z
);

  wire comparador_cero_4_1_z, not_1_out;

  not not_1 (not_1_out, A[4]);
  comparador_cero_4 comparador_cero_4_1 (.A(A[3:0]), .Z(comparador_cero_4_1_z));
  and and_1 (Z, comparador_cero_4_1_z, not_1_out);
endmodule

module uno_5_E24 (
  input  [4:0] A,
  output uno
);

  wire [0:0] not_1_out;

  not not_1 (not_1_out[0], A[0]);
  comparador_cero_5_E24 comparador_cero_5_e24_1 (.A({A[4:1], not_1_out[0]}), .Z(uno));
endmodule

module collatz_5_E24A (
  input  [4:0] A,
  output [4:0] S
);

  wire par_5_e24_1_p;
  wire [4:0] right_shifter_4_5_e24_1_s0, triplicador_incrementador_5_e24_1_s;

  triplicador_incrementador_5_E24 triplicador_incrementador_5_e24_1 (.A(A), .S(triplicador_incrementador_5_e24_1_s));
  right_shifter_4_5_E24 right_shifter_4_5_e24_1 (
    .e0(A[1]), .e1(A[2]), .e2(A[3]), .e3(A[4]), .c(1'b1), .s0(right_shifter_4_5_e24_1_s0[0]),
    .s1(right_shifter_4_5_e24_1_s0[1]), .s2(right_shifter_4_5_e24_1_s0[2]),
    .s3(right_shifter_4_5_e24_1_s0[3]), .s4(right_shifter_4_5_e24_1_s0[4]));
  par_5_E24 par_5_e24_1 (.A(A), .P(par_5_e24_1_p));
  Multiplexer #(.width(5)) multiplexer_1 (
    .in0(triplicador_incrementador_5_e24_1_s), .in1(right_shifter_4_5_e24_1_s0), .out(S), .sel(par_5_e24_1_p));
endmodule

module collatz_5_E24BC (
  output [4:0] S
);

  wire clock_1_out, multiplexer_1_out, multiplexer_2_out, multiplexer_3_out, multiplexer_4_out,
       multiplexer_5_out, not_1_out, uno_5_e24_1_uno;
  wire [4:0] d_ff_1_q;

  not not_1 (not_1_out, uno_5_e24_1_uno);
  D_Flip_Flop d_ff_1 (.D(multiplexer_1_out), .clk(clock_1_out), .Q(d_ff_1_q[0]));  // open: Qn, preset, reset
  Multiplexer multiplexer_1 (.in0(d_ff_1_q[0]), .in1(S[0]), .out(multiplexer_1_out), .sel(not_1_out));
  D_Flip_Flop d_ff_2 (.D(multiplexer_2_out), .clk(clock_1_out), .Q(d_ff_1_q[1]));  // open: Qn, preset, reset
  Multiplexer multiplexer_2 (.in0(d_ff_1_q[1]), .in1(S[1]), .out(multiplexer_2_out), .sel(not_1_out));
  D_Flip_Flop d_ff_3 (.D(multiplexer_3_out), .clk(clock_1_out), .Q(d_ff_1_q[2]));  // open: Qn, preset, reset
  Multiplexer multiplexer_3 (.in0(d_ff_1_q[2]), .in1(S[2]), .out(multiplexer_3_out), .sel(not_1_out));
  D_Flip_Flop d_ff_4 (.D(multiplexer_4_out), .clk(clock_1_out), .Q(d_ff_1_q[3]));  // open: Qn, preset, reset
  Multiplexer multiplexer_4 (.in0(d_ff_1_q[3]), .in1(S[3]), .out(multiplexer_4_out), .sel(not_1_out));
  D_Flip_Flop d_ff_5 (.D(multiplexer_5_out), .clk(clock_1_out), .Q(d_ff_1_q[4]));  // open: Qn, preset, reset
  Multiplexer multiplexer_5 (.in0(d_ff_1_q[4]), .in1(S[4]), .out(multiplexer_5_out), .sel(not_1_out));
  Clock clock_1 (.out(clock_1_out));
  collatz_5_E24A collatz_5_e24a_1 (.A(d_ff_1_q), .S(S));
  uno_5_E24 uno_5_e24_1 (.A(S), .uno(uno_5_e24_1_uno));
endmodule
