// Logisim project ALU4bit.circ as structural Verilog: 18 circuits, main circuit verificador
module sumador_simple_1 (
  input  A,
  input  B,
  output S,
  output Cout
);

  xor xor_1 (S, A, B);
  and and_1 (Cout, A, B);
endmodule

module sumador_completo_1 (
  input  Cin,
  input  A,
  input  B,
  output S,
  output Cout
);

  wire sumador_simple_1_1_cout, sumador_simple_1_1_s, sumador_simple_1_2_cout;

  sumador_simple_1 sumador_simple_1_1 (.A(A), .B(B), .S(sumador_simple_1_1_s), .Cout(sumador_simple_1_1_cout));
  sumador_simple_1 sumador_simple_1_2 (.A(sumador_simple_1_1_s), .B(Cin), .S(S), .Cout(sumador_simple_1_2_cout));
  or or_1 (Cout, sumador_simple_1_2_cout, sumador_simple_1_1_cout);
endmodule

module sumador_4 (
  input  Cin,
  input  [3:0] A,
  input  [3:0] B,
  output [3:0] S,
  output Cout
);

  wire sumador_completo_1_1_cout, sumador_completo_1_2_cout, sumador_completo_1_3_cout;

  sumador_completo_1 sumador_completo_1_1 (.Cin(Cin), .A(A[0]), .B(B[0]), .S(S[0]), .Cout(sumador_completo_1_1_cout));
  sumador_completo_1 sumador_completo_1_2 (
    .Cin(sumador_completo_1_1_cout), .A(A[1]), .B(B[1]), .S(S[1]), .Cout(sumador_completo_1_2_cout));
  sumador_completo_1 sumador_completo_1_3 (
    .Cin(sumador_completo_1_2_cout), .A(A[2]), .B(B[2]), .S(S[2]), .Cout(sumador_completo_1_3_cout));
  sumador_completo_1 sumador_completo_1_4 (.Cin(sumador_completo_1_3_cout), .A(A[3]), .B(B[3]), .S(S[3]), .Cout(Cout));
  Hex_Digit_Display hex_digit_display_1 (.value(S));  // open: dp
endmodule

module comparador_cero_4 (
  input  [3:0] A,
  output Z
);

  wire or_1_out, or_2_out, or_3_out;

  or or_1 (or_1_out, A[0], A[1]);
  or or_2 (or_2_out, A[2], A[3]);
  or or_3 (or_3_out, or_1_out, or_2_out);
  not not_1 (Z, or_3_out);
endmodule

module sumador_flags_4 (
  input  Cin,
  input  [3:0] A,
  input  [3:0] B,
  output V,
  output N,
  output [3:0] S,
  output Z,
  output C
);

  wire not_1_out, xor_1_out, xor_2_out;

  xor xor_1 (xor_1_out, A[3], B[3]);
  not not_1 (not_1_out, xor_1_out);
  sumador_4 sumador_4_1 (.Cin(Cin), .A(A), .B(B), .S({N, S[2:0]}), .Cout(C));
  xor xor_2 (xor_2_out, A[3], N);
  Hex_Digit_Display hex_digit_display_1 (.value({N, S[2:0]}));  // open: dp
  comparador_cero_4 comparador_cero_4_1 (.A({N, S[2:0]}), .Z(Z));
  and and_1 (V, xor_2_out, not_1_out);

  assign S[3] = N;
endmodule

module incrementador_4 (
  input  [3:0] A,
  output [3:0] S
);

  sumador_4 sumador_4_1 (.Cin(1'b0), .A(A), .B(4'b0001), .S(S));  // open: Cout
  Hex_Digit_Display hex_digit_display_1 (.value(S));  // open: dp
endmodule

module inversor_4 (
  input  [3:0] A,
  input  INV,
  output [3:0] S
);

  wire [3:0] incrementador_4_1_s, xor_1_out;

  xor xor_1 (xor_1_out[0], A[0], INV);
  xor xor_2 (xor_1_out[1], A[1], INV);
  xor xor_3 (xor_1_out[2], A[2], INV);
  xor xor_4 (xor_1_out[3], A[3], INV);
  incrementador_4 incrementador_4_1 (.A(xor_1_out), .S(incrementador_4_1_s));
  Multiplexer #(.width(4)) multiplexer_1 (.in0(A), .in1(incrementador_4_1_s), .out(S), .sel(INV));
  Hex_Digit_Display hex_digit_display_1 (.value(S));  // open: dp
endmodule

module or_4 (
  input  [3:0] A,
  input  [3:0] B,
  output [3:0] S
);

  or or_1 (S[0], B[0], A[0]);
  or or_2 (S[1], B[1], A[1]);
  or or_3 (S[2], B[2], A[2]);
  or or_4 (S[3], B[3], A[3]);
endmodule

module and_4 (
  input  [3:0] A,
  input  [3:0] B,
  output [3:0] S
);

  and and_1 (S[0], B[0], A[0]);
  and and_2 (S[1], B[1], A[1]);
  and and_3 (S[2], B[2], A[2]);
  and and_4 (S[3], B[3], A[3]);
endmodule

module neg_4 (
  input  [3:0] A,
  output N
);


  assign N = A[3];
endmodule

module menos_8_4 (
  input  [3:0] B,
  output menos8
);

  wire [3:3] not_1_out;

  not not_1 (not_1_out[3], B[3]);
  comparador_cero_4 comparador_cero_4_1 (.A({not_1_out[3], B[2:0]}), .Z(menos8));
endmodule

module ALU_4 (
  input  [3:0] A,
  input  [3:0] B,
  input  [1:0] OP,
  output V,
  output C,
  output [3:0] S,
  output N,
  output Z
);

  wire and_1_out, and_2_out, and_3_out, and_4_out, and_5_out, and_6_out, and_7_out, and_8_out,
       comparador_cero_4_1_z, menos_8_4_1_menos8, neg_4_1_n, not_1_out, not_2_out, not_3_out, not_4_out,
       sumador_flags_4_1_c, sumador_flags_4_1_v, xor_1_out;
  wire [3:0] and_4_1_s, inversor_4_1_s, or_4_1_s, sumador_flags_4_1_s;

  neg_4 neg_4_1 (.A(A), .N(neg_4_1_n));
  menos_8_4 menos_8_4_1 (.B(B), .menos8(menos_8_4_1_menos8));
  not not_1 (not_1_out, neg_4_1_n);
  inversor_4 inversor_4_1 (.A(B), .INV(OP[0]), .S(inversor_4_1_s));
  and and_1 (and_1_out, neg_4_1_n, menos_8_4_1_menos8);
  and and_2 (and_2_out, not_1_out, menos_8_4_1_menos8);
  not not_2 (not_2_out, comparador_cero_4_1_z);
  comparador_cero_4 comparador_cero_4_1 (.A(B), .Z(comparador_cero_4_1_z));
  and_4 and_4_1 (.A(A), .B(B), .S(and_4_1_s));
  or_4 or_4_1 (.A(A), .B(B), .S(or_4_1_s));
  and and_3 (and_3_out, and_1_out, OP[0]);
  not not_3 (not_3_out, and_3_out);
  and and_4 (and_4_out, and_2_out, OP[0]);
  Multiplexer #(.select(2), .width(4)) multiplexer_1 (
    .in0(sumador_flags_4_1_s), .in1(sumador_flags_4_1_s), .in2(and_4_1_s), .in3(or_4_1_s), .out(S), .sel(OP));
  sumador_flags_4 sumador_flags_4_1 (
    .Cin(1'b0), .A(A), .B(inversor_4_1_s), .V(sumador_flags_4_1_v), .S(sumador_flags_4_1_s),
    .C(sumador_flags_4_1_c));  // open: N, Z
  xor xor_1 (xor_1_out, sumador_flags_4_1_c, OP[0]);
  not not_4 (not_4_out, OP[1]);
  and and_5 (and_5_out, not_4_out, and_4_out);
  and and_6 (and_6_out, not_4_out, sumador_flags_4_1_v);
  and and_7 (and_7_out, not_3_out, and_6_out);
  and and_8 (and_8_out, xor_1_out, not_4_out);
  Hex_Digit_Display hex_digit_display_1 (.value(S));  // open: dp
  neg_4 neg_4_2 (.A(S), .N(N));
  comparador_cero_4 comparador_cero_4_2 (.A(S), .Z(Z));
  or or_1 (V, and_7_out, and_5_out);
  and and_9 (C, and_8_out, not_2_out);
endmodule

module igualdad_4 (
  input  [3:0] A,
  input  [3:0] B,
  output I
);

  wire and_1_out, and_2_out, not_1_out, not_2_out, not_3_out, not_4_out, xor_1_out, xor_2_out, xor_3_out,
       xor_4_out;

  xor xor_1 (xor_1_out, B[0], A[0]);
  not not_1 (not_1_out, xor_1_out);
  xor xor_2 (xor_2_out, B[1], A[1]);
  not not_2 (not_2_out, xor_2_out);
  xor xor_3 (xor_3_out, B[2], A[2]);
  not not_3 (not_3_out, xor_3_out);
  xor xor_4 (xor_4_out, B[3], A[3]);
  not not_4 (not_4_out, xor_4_out);
  and and_1 (and_1_out, not_1_out, not_2_out);
  and and_2 (and_2_out, not_3_out, not_4_out);
  and and_3 (I, and_1_out, and_2_out);
endmodule

module a_mayor_b_sin_signo (
  input  [3:0] A,
  input  [3:0] B,
  output G
);

  wire and_1_out, and_2_out, and_3_out, and_4_out, and_5_out, and_6_out, and_7_out, and_8_out, and_9_out,
       not_1_out, not_2_out, not_3_out, not_4_out, not_5_out, not_6_out, not_7_out, or_1_out, or_2_out,
       xor_1_out, xor_2_out, xor_3_out;

  not not_1 (not_1_out, B[3]);
  not not_2 (not_2_out, B[2]);
  not not_3 (not_3_out, B[1]);
  not not_4 (not_4_out, B[0]);
  xor xor_1 (xor_1_out, B[3], A[3]);
  not not_5 (not_5_out, xor_1_out);
  and and_1 (and_1_out, not_2_out, A[2]);
  xor xor_2 (xor_2_out, B[2], A[2]);
  not not_6 (not_6_out, xor_2_out);
  and and_2 (and_2_out, not_3_out, A[1]);
  xor xor_3 (xor_3_out, B[1], A[1]);
  not not_7 (not_7_out, xor_3_out);
  and and_3 (and_3_out, not_4_out, A[0]);
  and and_4 (and_4_out, not_5_out, not_6_out);
  and and_5 (and_5_out, and_4_out, not_7_out);
  and and_6 (and_6_out, not_1_out, A[3]);
  and and_7 (and_7_out, not_5_out, and_1_out);
  and and_8 (and_8_out, and_4_out, and_2_out);
  and and_9 (and_9_out, and_5_out, and_3_out);
  or or_1 (or_1_out, and_6_out, and_7_out);
  or or_2 (or_2_out, and_8_out, and_9_out);
  or or_3 (G, or_1_out, or_2_out);
endmodule

module a_mayorigual_b_sin_signo (
  input  [3:0] A,
  input  [3:0] B,
  output GE
);

  wire a_mayor_b_sin_signo_1_g, igualdad_4_1_i;

  a_mayor_b_sin_signo a_mayor_b_sin_signo_1 (.A(A), .B(B), .G(a_mayor_b_sin_signo_1_g));
  igualdad_4 igualdad_4_1 (.A(A), .B(B), .I(igualdad_4_1_i));
  or or_1 (GE, a_mayor_b_sin_signo_1_g, igualdad_4_1_i);
endmodule

module detector_OF_sin_signo_4 (
  input  [3:0] B,
  input  [3:0] A,
  input  R,
  output V
);

  wire a_mayor_b_sin_signo_1_g, a_mayorigual_b_sin_signo_1_ge, and_1_out, comparador_cero_4_1_z, not_1_out,
       not_2_out;
  wire [3:0] inversor_4_1_s;

  not not_1 (not_1_out, R);
  inversor_4 inversor_4_1 (.A(B), .INV(not_1_out), .S(inversor_4_1_s));
  comparador_cero_4 comparador_cero_4_1 (.A(B), .Z(comparador_cero_4_1_z));
  a_mayorigual_b_sin_signo a_mayorigual_b_sin_signo_1 (.A(A), .B(inversor_4_1_s), .GE(a_mayorigual_b_sin_signo_1_ge));
  a_mayor_b_sin_signo a_mayor_b_sin_signo_1 (.A(B), .B(A), .G(a_mayor_b_sin_signo_1_g));
  not not_2 (not_2_out, comparador_cero_4_1_z);
  and and_1 (and_1_out, not_2_out, a_mayorigual_b_sin_signo_1_ge);
  Multiplexer multiplexer_1 (.in0(and_1_out), .in1(a_mayor_b_sin_signo_1_g), .out(V), .sel(R));
endmodule

module detector_OF_sin_signo_eficiente_4 (
  input  R,
  input  [3:0] A,
  input  [3:0] B,
  output V
);

  wire a_mayor_b_sin_signo_1_g, and_1_out, and_2_out, and_3_out, and_4_out, comparador_cero_4_1_z,
       igualdad_4_1_i, not_1_out, not_2_out, not_3_out, or_1_out;
  wire [3:0] inversor_4_1_s, multiplexer_1_out, multiplexer_2_out;

  not not_1 (not_1_out, R);
  Multiplexer #(.width(4)) multiplexer_1 (.in0(A), .in1(B), .out(multiplexer_1_out), .sel(R));
  Multiplexer #(.width(4)) multiplexer_2 (.in0(inversor_4_1_s), .in1(A), .out(multiplexer_2_out), .sel(R));
  inversor_4 inversor_4_1 (.A(B), .INV(not_1_out), .S(inversor_4_1_s));
  igualdad_4 igualdad_4_1 (.A(A), .B(inversor_4_1_s), .I(igualdad_4_1_i));
  comparador_cero_4 comparador_cero_4_1 (.A(B), .Z(comparador_cero_4_1_z));
  a_mayor_b_sin_signo a_mayor_b_sin_signo_1 (.A(multiplexer_1_out), .B(multiplexer_2_out), .G(a_mayor_b_sin_signo_1_g));
  not not_2 (not_2_out, comparador_cero_4_1_z);
  not not_3 (not_3_out, R);
  and and_1 (and_1_out, a_mayor_b_sin_signo_1_g, R);
  and and_2 (and_2_out, a_mayor_b_sin_signo_1_g, not_3_out);
  and and_3 (and_3_out, igualdad_4_1_i, not_3_out);
  or or_1 (or_1_out, and_2_out, and_3_out);
  and and_4 (and_4_out, or_1_out, not_2_out);
  or or_2 (V, and_1_out, and_4_out);
endmodule

module verificador (
  output [3:0] out_1,
  output [3:0] out_2,
  output [1:0] out_3,
  output halt,
  output N,
  output Z,
  output V,
  output C,
  output [3:0] res
);

  wire clock_1_out;

  Clock clock_1 (.out(clock_1_out));
  Counter #(.max('h3ff), .width(10)) counter_1 (
    .clk(clock_1_out), .carry(halt), .Q({out_3, out_2, out_1}));  // open: clr, load, up, count, D
  ALU_4 alu_4_1 (.A(out_1), .B(out_2), .OP(out_3), .V(V), .C(C), .S(res), .N(N), .Z(Z));
endmodule
