// Logisim project taller02.circ as structural Verilog: 6 circuits, main circuit buffer_tres_estados
module buffer_tres_estados (
  input  A,
  input  A_en,
  input  B,
  input  B_en,
  input  C,
  input  C_en,
  output Res
);

  assign Res = A_en ? A : 1'bz;  // Controlled_Buffer controlled_buffer_1
  assign Res = B_en ? B : 1'bz;  // Controlled_Buffer controlled_buffer_2
  assign Res = C_en ? C : 1'bz;  // Controlled_Buffer controlled_buffer_3
endmodule

module registro_salida_restringida (
  input  clk,
  input  Reg_in,
  input  w,
  input  en_out,
  output Reg_Debug,
  output Reg_output
);

  wire multiplexer_1_out;

  D_Flip_Flop d_ff_1 (.D(multiplexer_1_out), .clk(clk), .Q(Reg_Debug));  // open: Qn, preset, reset
  Multiplexer multiplexer_1 (.in0(Reg_Debug), .in1(Reg_in), .out(multiplexer_1_out), .sel(w));
  assign Reg_output = en_out ? Reg_Debug : 1'bz;  // Controlled_Buffer controlled_buffer_1
endmodule

module registro_4bytes_salida (
  input  [3:0] Reg4_in,
  input  clk,
  input  w,
  input  en_out,
  output [3:0] Reg4_Debug,
  output [3:0] Reg4_output
);

  registro_salida_restringida registro_salida_restringida_1 (
    .clk(clk), .Reg_in(Reg4_in[0]), .w(w), .en_out(en_out), .Reg_Debug(Reg4_Debug[0]),
    .Reg_output(Reg4_output[0]));
  registro_salida_restringida registro_salida_restringida_2 (
    .clk(clk), .Reg_in(Reg4_in[1]), .w(w), .en_out(en_out), .Reg_Debug(Reg4_Debug[1]),
    .Reg_output(Reg4_output[1]));
  registro_salida_restringida registro_salida_restringida_3 (
    .clk(clk), .Reg_in(Reg4_in[2]), .w(w), .en_out(en_out), .Reg_Debug(Reg4_Debug[2]),
    .Reg_output(Reg4_output[2]));
  registro_salida_restringida registro_salida_restringida_4 (
    .clk(clk), .Reg_in(Reg4_in[3]), .w(w), .en_out(en_out), .Reg_Debug(Reg4_Debug[3]),
    .Reg_output(Reg4_output[3]));
endmodule

module ALU_regs (
  input  clk,
  input  [3:0] A,
  input  A_Write,
  input  [3:0] B,
  input  B_Write,
  input  in_6,
  input  [1:0] OP,
  output [3:0] A_Debug,
  output [3:0] B_Debug,
  output N,
  output Z,
  output V,
  output C,
  output [3:0] S_Debug,
  output [3:0] Reg4_output
);

  wire not_1_out;
  wire [3:0] alu_4_1_s, registro_4bytes_salida_1_reg4_output, registro_4bytes_salida_2_reg4_output;

  registro_4bytes_salida registro_4bytes_salida_1 (
    .Reg4_in(A), .clk(clk), .w(A_Write), .en_out(1'b1), .Reg4_Debug(A_Debug),
    .Reg4_output(registro_4bytes_salida_1_reg4_output));
  registro_4bytes_salida registro_4bytes_salida_2 (
    .Reg4_in(B), .clk(clk), .w(B_Write), .en_out(1'b1), .Reg4_Debug(B_Debug),
    .Reg4_output(registro_4bytes_salida_2_reg4_output));
  not not_1 (not_1_out, clk);
  ALU_4 alu_4_1 (
    .A(registro_4bytes_salida_1_reg4_output), .B(registro_4bytes_salida_2_reg4_output), .OP(OP), .V(V),
    .C(C), .S(alu_4_1_s), .N(N), .Z(Z));
  registro_4bytes_salida registro_4bytes_salida_3 (
    .Reg4_in(alu_4_1_s), .clk(not_1_out), .w(1'b1), .en_out(in_6), .Reg4_Debug(S_Debug),
    .Reg4_output(Reg4_output));
endmodule

module ej_02 (
  input  w_R0,
  input  en_out_R0,
  input  w_R1,
  input  en_out_R1,
  input  clk,
  input  Force_Input,
  input  w_R2,
  input  en_out_R2,
  input  en_Force_Input,
  output R0,
  output bus_1,
  output R1,
  output R2
);

  assign bus_1 = en_Force_Input ? Force_Input : 1'bz;  // Controlled_Buffer controlled_buffer_1
  registro_salida_restringida registro_salida_restringida_1 (
    .clk(clk), .Reg_in(bus_1), .w(w_R0), .en_out(en_out_R0), .Reg_Debug(R0), .Reg_output(bus_1));
  registro_salida_restringida registro_salida_restringida_2 (
    .clk(clk), .Reg_in(bus_1), .w(w_R1), .en_out(en_out_R1), .Reg_Debug(R1), .Reg_output(bus_1));
  registro_salida_restringida registro_salida_restringida_3 (
    .clk(clk), .Reg_in(bus_1), .w(w_R2), .en_out(en_out_R2), .Reg_Debug(R2), .Reg_output(bus_1));
endmodule

module ej_03 (
  input  clk,
  input  ALU_A_Write,
  input  ALU_B_Write,
  input  [1:0] OP,
  input  ALU_enableOut,
  input  Reg0_Write,
  input  Reg0_enableOut,
  input  Reg1_Write,
  input  Reg1_enableOut,
  input  Reg2_Write,
  input  Reg2_enableOut,
  input  Reg3_Write,
  input  Reg3_enableOut,
  input  [3:0] Force_Input,
  input  en_Force_Input,
  output N,
  output Z,
  output V,
  output C
);

  wire [3:0] alu_regs_1_a_debug, alu_regs_1_b_debug, alu_regs_1_s_debug, controlled_buffer_1_out,
       Registro_00_reg4_debug, Registro_00_reg4_output, Registro_01_reg4_debug, Registro_02_reg4_debug,
       Registro_03_reg4_debug;

  assign controlled_buffer_1_out = en_Force_Input ? Force_Input : 4'bz;  // Controlled_Buffer controlled_buffer_1
  Hex_Digit_Display hex_digit_display_1 (.value(Registro_00_reg4_debug));  // open: dp
  registro_4bytes_salida Registro_00 (
    .Reg4_in(controlled_buffer_1_out), .clk(clk), .w(Reg0_Write), .en_out(Reg0_enableOut),
    .Reg4_Debug(Registro_00_reg4_debug), .Reg4_output(Registro_00_reg4_output));
  Hex_Digit_Display hex_digit_display_2 (.value(Registro_01_reg4_debug));  // open: dp
  registro_4bytes_salida Registro_01 (
    .Reg4_in(controlled_buffer_1_out), .clk(clk), .w(Reg1_Write), .en_out(Reg1_enableOut),
    .Reg4_Debug(Registro_01_reg4_debug), .Reg4_output(Registro_00_reg4_output));
  Hex_Digit_Display hex_digit_display_3 (.value(Registro_02_reg4_debug));  // open: dp
  registro_4bytes_salida Registro_02 (
    .Reg4_in(controlled_buffer_1_out), .clk(clk), .w(Reg2_Write), .en_out(Reg2_enableOut),
    .Reg4_Debug(Registro_02_reg4_debug), .Reg4_output(Registro_00_reg4_output));
  Hex_Digit_Display hex_digit_display_4 (.value(Registro_03_reg4_debug));  // open: dp
  registro_4bytes_salida Registro_03 (
    .Reg4_in(controlled_buffer_1_out), .clk(clk), .w(Reg3_Write), .en_out(Reg3_enableOut),
    .Reg4_Debug(Registro_03_reg4_debug), .Reg4_output(Registro_00_reg4_output));
  ALU_regs alu_regs_1 (
    .A(Registro_00_reg4_output), .A_Write(ALU_A_Write), .B(Registro_00_reg4_output), .B_Write(ALU_B_Write),
    .clk(clk), .OP(OP), .in_6(ALU_enableOut), .S_Debug(alu_regs_1_s_debug),
    .Reg4_output(controlled_buffer_1_out), .A_Debug(alu_regs_1_a_debug), .B_Debug(alu_regs_1_b_debug), .N(N),
    .Z(Z), .V(V), .C(C));
  Hex_Digit_Display hex_digit_display_5 (.value(alu_regs_1_a_debug));  // open: dp
  Hex_Digit_Display hex_digit_display_6 (.value(alu_regs_1_b_debug));  // open: dp
  Hex_Digit_Display hex_digit_display_7 (.value(alu_regs_1_s_debug));  // open: dp
endmodule
